# Fritzing sketch Power source regulator (saved by Fritzing 0.9.5d)
circuit board: 4.50383cm x 2.65289cm
breadboards: 1

parts:
  U1 = Voltage Regulator - 5V [package="TO220 [THT]"]
  C3 = Electrolytic Capacitor [capacitance=470µF package="100 mil [THT, electrolytic]"]
  C2 = Ceramic Capacitor [capacitance=100nF package="100 mil [THT, multilayer]"]
  C1 = Ceramic Capacitor [capacitance=0.22µF package="100 mil [THT, multilayer]"]
  D1 = Rectifier Diode [part_number=1N4001 package="300 mil [THT]"]
  D2 = Schottky Diode [part_number=1N5817 package="300 mil [THT]"]
  D3 = Schottky Diode [part_number=1N5817 package="300 mil [THT]"]
  Power = female pin header, 2 pins [form="♀ (female)"]
  LED_driver = female pin header, 2 pins [form="♀ (female)"]
  Teensy_Vcc = female pin header, 2 pins [form="♀ (female)"]
  XFM2_Vcc = female pin header, 2 pins [form="♀ (female)"]

nets:
  N1: U1.input_voltage, C1.1, D1.cathode
  GND: U1.GND, C3.-, C2.0, C1.0, Power.pin1, LED_driver.pin2, Teensy_Vcc.pin2, XFM2_Vcc.pin2
  N2: U1.output_voltage, C3.+, C2.1, D2.anode, D3.anode, LED_driver.pin1
  N3: D1.anode, Power.pin2
  N4: D2.cathode, XFM2_Vcc.pin1
  N5: D3.cathode, Teensy_Vcc.pin1

notes:
  470uF low frequency output filter and power buffer
  100nF high frequency output filter
  220nF (=0,22uF) input filter for regulator
  diode for reverse polarity protection
  Skotty diodes to seperate current from USB of both devices
  Actual voltage is 5V minus drop of diode.
  All outputs have a separate ground connector
