# Fritzing sketch XFM2 (saved by Fritzing 0.9.5d)
circuit board: 6cm x 8cm
breadboards: 1

parts:
  Cmod_A7 = Cmod A7
  U1 = Optocoupler [package=THT]
  R1 = Resistor [tolerance=±5% resistance=220 package=THT]
  R2 = Resistor [tolerance=±5% resistance=470 package=THT]
  EEPROM = IC, DIP package, 8 pins [chip_label=IC]
  UDA1334a = Adafruit UDA1334 I2S DAC
  D1 = Diode [package=diode-1n4148]
  to_Power = female pin header, 2 pins [form="♀ (female)"]
  Audio_out = female pin header, 3 pins [form="♀ (female)"]
  to_Teensy = female pin header, 2 pins [form="♀ (female)"]
  Midi_in = female pin header, 2 pins [form="♀ (female)"]

nets:
  Vcc: Cmod_A7.VU, to_Power.pin1
  N1: Cmod_A7.GND, to_Power.pin2
  TX: Cmod_A7.D26, to_Teensy.pin1
  RX: Cmod_A7.D27, to_Teensy.pin2
  SCK: Cmod_A7.D31, UDA1334a.BITCLK_IN
  SDA: Cmod_A7.D32, UDA1334a.DATA_IN
  WSel: Cmod_A7.D33, UDA1334a.WORDSEL_IN
  N2: Cmod_A7.D34, UDA1334a.GND
  MUTE: Cmod_A7.D35, UDA1334a.MUTE
  VIN: Cmod_A7.D36, UDA1334a.SFOR1, UDA1334a.SFOR0, UDA1334a.VIN
  N3: Cmod_A7.D42, U1.Pin_5, R2.Pin_1
  N4: Cmod_A7.D43, U1.Pin_4
  N5: Cmod_A7.D45, R2.Pin_0, EEPROM.pin3, EEPROM.pin8
  GNDe: Cmod_A7.D46, EEPROM.pin1, EEPROM.pin2, EEPROM.pin4, EEPROM.pin7
  N6: Cmod_A7.D47, EEPROM.pin6
  N7: Cmod_A7.D48, EEPROM.pin5
  N8: U1.Pin_1, R1.Pin_1, D1.C
  N9: U1.Pin_2, D1.A, Midi_in.pin2
  N10: R1.Pin_0, Midi_in.pin1
  N11: UDA1334a.OUTL, Audio_out.pin3
  N12: UDA1334a.AGND, Audio_out.pin2
  N13: UDA1334a.OUTR, Audio_out.pin1

custom parts:
  Cmod A7: The Digilent Cmod A7 is a small, 48-pin DIP form factor board built around a Xilinx Artix 7 FPGA. The board also includes a USB-JTAG programming circuit, USB-UART bridge, clock source, Pmod host connector, SRAM, Quad SPI Flash, and basic I/O devices. These components make it a formidable, albeit compact, platform for digital logic circuits and Microblaze embedded softcore processor designs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
  Adafruit UDA1334 I2S DAC: This fully-featured UDA1334A I2S Stereo DAC breakout is a perfect match for any I2S-output audio interface. It's affordable but sounds great! The NXP UDA1334A is a jack-of-all-I2S-trades: you can use 3.3V - 5V logic levels (a rarity), and can process multiple different formats by setting two pins to high or low. The DAC will process data immediately, and give you a clear, analog, stereo line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
