# Fritzing sketch buttons-blue-ic (saved by Fritzing 0.9.5d)
circuit board: 5.01969cm x 12.0339cm
breadboards: 1

parts:
  Onderdeel1 = LED Tactile Button 12mm [part_number=BOB-10467]
  Onderdeel2 = LED Tactile Button 12mm [part_number=BOB-10467]
  Onderdeel3 = LED Tactile Button 12mm [part_number=BOB-10467]
  Onderdeel4 = LED Tactile Button 12mm [part_number=BOB-10467]
  Onderdeel5 = LED Tactile Button 12mm [part_number=BOB-10467]
  Onderdeel6 = LED Tactile Button 12mm [part_number=BOB-10467]
  IC1 = IC, DIP package, 24 pins [chip_label=IC]
  R2 = Resistor [tolerance=±5% resistance=220 package=THT]
  R3 = Resistor [tolerance=±5% resistance=220 package=THT]
  R4 = Resistor [tolerance=±5% resistance=220 package=THT]
  R5 = Resistor [tolerance=±5% resistance=220 package=THT]
  R6 = Resistor [tolerance=±5% resistance=220 package=THT]
  IC2 = IC, DIP package, 14 pins [chip_label=IC]
  P2 = female pin header, 8 pins [form="♀ (female)"]
  P3 = female pin header, 8 pins [form="♀ (female)"]
  P4 = female pin header, 8 pins [form="♀ (female)"]
  P5 = female pin header, 8 pins [form="♀ (female)"]
  P6 = female pin header, 8 pins [form="♀ (female)"]
  R7 = Resistor [tolerance=±5% resistance=10k package=THT]
  J2 = female pin header, 2 pins [form="♀ (female)"]
  R8 = Resistor [tolerance=±5% resistance=220 package=THT]
  J4 = female pin header, 6 pins [form="♀ (female)"]

nets:
  N1: Onderdeel1.pin_1, IC1.pin21
  N2: Onderdeel1.pin_2, Onderdeel2.pin_2, Onderdeel3.pin_2, Onderdeel4.pin_2, Onderdeel5.pin_2, Onderdeel6.pin_2, IC1.pin2
  N3: Onderdeel1.pin_3, Onderdeel1.pin_5, Onderdeel2.pin_3, Onderdeel2.pin_5, Onderdeel3.pin_3, Onderdeel3.pin_5, Onderdeel4.pin_3, Onderdeel4.pin_5, Onderdeel5.pin_3, Onderdeel5.pin_5, Onderdeel6.pin_3, Onderdeel6.pin_5, J4.pin1
  N4: Onderdeel1.pin_4, Onderdeel1.pin_6, R5.Pin_1, R8.Pin_0
  N5: Onderdeel2.pin_1, IC1.pin17
  N6: Onderdeel2.pin_4, Onderdeel2.pin_6, R4.Pin_1, R5.Pin_0
  N7: Onderdeel3.pin_1, IC1.pin20
  N8: Onderdeel3.pin_4, Onderdeel3.pin_6, R4.Pin_0, R6.Pin_1
  N9: Onderdeel4.pin_1, IC1.pin16, P3.pin8, P4.pin8, P5.pin8
  N10: Onderdeel4.pin_4, Onderdeel4.pin_6, R3.Pin_1, R6.Pin_0
  N11: Onderdeel5.pin_1, IC1.pin14, P2.pin6, P3.pin6, P4.pin6, P5.pin6, P6.pin6
  N12: Onderdeel5.pin_4, Onderdeel5.pin_6, R2.Pin_1, R3.Pin_0
  N13: Onderdeel6.pin_1, IC1.pin15, P2.pin7, P3.pin7, P4.pin7, P5.pin7, P6.pin7
  N14: Onderdeel6.pin_4, Onderdeel6.pin_6, R2.Pin_0, P2.pin5, P3.pin5, P4.pin5, P5.pin5, P6.pin5, J4.pin6
  N15: IC1.pin1, IC2.pin6
  N16: IC1.pin4, IC2.pin1, IC2.pin4, IC2.pin7, IC2.pin10, J2.pin1
  N17: IC1.pin12, IC2.pin3
  N18: IC1.pin13, IC2.pin8
  N19: IC1.pin18, IC2.pin14, R7.Pin_0, J2.pin2
  N20: IC1.pin19, R7.Pin_1
  N21: IC2.pin2, J4.pin5
  N22: IC2.pin5, J4.pin4
  N23: IC2.pin9, J4.pin3
  N24: P2.pin2, P3.pin2, P4.pin2, P5.pin2, P6.pin2
  N25: P2.pin3, P3.pin3, P4.pin3, P5.pin3, P6.pin3
  N26: P2.pin4, P3.pin4, P4.pin4, P5.pin4, P6.pin4
  N27: R8.Pin_1, J4.pin2

custom parts:
  LED Tactile Button 12mm: A LED tactile switch
