# Fritzing sketch buttons-red-ic (saved by Fritzing 0.9.5d)
circuit board: 10.3598cm x 4.42098cm
breadboards: 1

parts:
  Onderdeel7 = LED Tactile Button 12mm [part_number=BOB-10467]
  Onderdeel8 = LED Tactile Button 12mm [part_number=BOB-10467]
  Onderdeel9 = LED Tactile Button 12mm [part_number=BOB-10467]
  Onderdeel10 = LED Tactile Button 12mm [part_number=BOB-10467]
  Onderdeel11 = LED Tactile Button 12mm [part_number=BOB-10467]
  R1 = Resistor [tolerance=±5% resistance=2.2k package=THT]
  R2 = Resistor [tolerance=±5% resistance=2.2k package=THT]
  R3 = Resistor [tolerance=±5% resistance=2.2k package=THT]
  R4 = Resistor [tolerance=±5% resistance=2.2k package=THT]
  R5 = Resistor [tolerance=±5% resistance=220 package=THT]
  IC1 = IC, DIP package, 24 pins [chip_label=IC]

nets:
  N1: Onderdeel7.pin_1, IC1.pin23
  N2: Onderdeel7.pin_2, Onderdeel8.pin_2, Onderdeel10.pin_2, Onderdeel11.pin_2, IC1.pin2
  N3: Onderdeel7.pin_3, Onderdeel7.pin_5, R1.Pin_0, R5.Pin_1
  N4: Onderdeel7.pin_4, Onderdeel7.pin_6, Onderdeel8.pin_4, Onderdeel8.pin_6, Onderdeel9.pin_4, Onderdeel9.pin_6, Onderdeel10.pin_4, Onderdeel10.pin_6, Onderdeel11.pin_6
  N5: Onderdeel8.pin_1, IC1.pin22
  N6: Onderdeel8.pin_3, Onderdeel8.pin_5, R1.Pin_1, R2.Pin_0
  N7: Onderdeel9.pin_1, IC1.pin21
  N8: Onderdeel9.pin_3, Onderdeel9.pin_5, R2.Pin_1, R3.Pin_0
  N9: Onderdeel10.pin_1, IC1.pin15
  N10: Onderdeel10.pin_3, Onderdeel10.pin_5, R3.Pin_1, R4.Pin_0
  N11: Onderdeel11.pin_1, IC1.pin14
  N12: Onderdeel11.pin_5, R4.Pin_1

notes:
  digit
  analog in
  GND
  vdd
  segA
  segB
  segC
  segD
  segE

custom parts:
  LED Tactile Button 12mm: A LED tactile switch
