# Fritzing sketch buttons-red (saved by Fritzing 0.9.5d)
circuit board: 10cm x 2.2cm
breadboards: 1

parts:
  sw_E = LED Tactile Button 12mm
  sw_G = LED Tactile Button 12mm
  sw_F = LED Tactile Button 12mm
  sw_A = LED Tactile Button 12mm
  sw_B = LED Tactile Button 12mm
  R1 = Resistor [tolerance=±5% resistance=2.2k package=THT]
  R2 = Resistor [tolerance=±5% resistance=2.2k package=THT]
  R3 = Resistor [tolerance=±5% resistance=2.2k package=THT]
  R4 = Resistor [tolerance=±5% resistance=2.2k package=THT]
  R5 = Resistor [tolerance=±5% resistance=220 package=THT]
  to_Teensy = female pin header, 2 pins [form="♀ (female)"]
  to_panel_#1 = female pin header, 8 pins [form="♀ (female)"]

nets:
  SEGE: sw_E.pin_1, to_panel_#1.pin2
  DIG1: sw_E.pin_2, sw_G.pin_2, sw_F.pin_2, sw_A.pin_2, sw_B.pin_2, to_panel_#1.pin1
  N1: sw_E.pin_3, sw_E.pin_5, R1.Pin_0, R5.Pin_1
  Btn-P2: sw_E.pin_4, sw_E.pin_6, sw_G.pin_4, sw_G.pin_6, sw_F.pin_4, sw_F.pin_6, sw_A.pin_4, sw_A.pin_6, sw_B.pin_4, sw_B.pin_6, to_Teensy.pin1
  SEGG: sw_G.pin_1, to_panel_#1.pin3
  N2: sw_G.pin_3, sw_G.pin_5, R1.Pin_1, R2.Pin_0
  SEGF: sw_F.pin_1, to_panel_#1.pin7
  N3: sw_F.pin_3, sw_F.pin_5, R2.Pin_1, R3.Pin_0
  SEGA: sw_A.pin_1, to_panel_#1.pin6
  N4: sw_A.pin_3, sw_A.pin_5, R3.Pin_1, R4.Pin_0
  SEGB: sw_B.pin_1, to_panel_#1.pin8
  3.3V: sw_B.pin_3, sw_B.pin_5, R4.Pin_1, to_panel_#1.pin5
  GND: R5.Pin_0, to_Teensy.pin2
  SEGC: to_panel_#1.pin4

notes:
  digit
  analog in
  GND

custom parts:
  LED Tactile Button 12mm: A LED tactile switch
