# Fritzing sketch buttons-yellow-top (saved by Fritzing 0.9.5d)
circuit board: 5.8889cm x 5.92145cm
breadboards: 1

parts:
  Onderdeel27 = LED Tactile Button 12mm [part_number=BOB-10467]
  Onderdeel28 = LED Tactile Button 12mm [part_number=BOB-10467]
  Onderdeel29 = LED Tactile Button 12mm [part_number=BOB-10467]
  Onderdeel30 = LED Tactile Button 12mm [part_number=BOB-10467]
  Onderdeel31 = LED Tactile Button 12mm [part_number=BOB-10467]
  Onderdeel32 = LED Tactile Button 12mm [part_number=BOB-10467]
  R18 = Resistor [tolerance=±5% resistance=1.5k package=THT]
  R19 = Resistor [tolerance=±5% resistance=1.5k package=THT]
  R20 = Resistor [tolerance=±5% resistance=1.5k package=THT]
  R21 = Resistor [tolerance=±5% resistance=1.5k package=THT]
  R22 = Resistor [tolerance=±5% resistance=220 package=THT]
  R23 = Resistor [tolerance=±5% resistance=1.5k package=THT]

nets:
  N1: Onderdeel27.pin_1, Onderdeel28.pin_1, Onderdeel29.pin_1, Onderdeel30.pin_1, Onderdeel31.pin_1, Onderdeel32.pin_1
  N2: Onderdeel27.pin_3, Onderdeel28.pin_3, Onderdeel28.pin_5, Onderdeel29.pin_3, Onderdeel29.pin_5, Onderdeel30.pin_3, Onderdeel31.pin_3, Onderdeel31.pin_5, Onderdeel32.pin_3
  N3: Onderdeel27.pin_4, Onderdeel27.pin_6, R18.Pin_0, R23.Pin_0
  N4: Onderdeel28.pin_4, Onderdeel28.pin_6, R18.Pin_1, R19.Pin_0
  N5: Onderdeel29.pin_4, Onderdeel29.pin_6, R19.Pin_1, R21.Pin_0
  N6: Onderdeel30.pin_4, Onderdeel30.pin_6, R20.Pin_0, R21.Pin_1
  N7: Onderdeel31.pin_4, Onderdeel31.pin_6, R20.Pin_1, R22.Pin_0
  N8: Onderdeel32.pin_4, Onderdeel32.pin_6, R22.Pin_1

notes:
  digit
  analog in
  GND
  Vdd
  segA
  segB
  segC
  segD
  segE
  segF

custom parts:
  LED Tactile Button 12mm: A LED tactile switch
