# Fritzing sketch buttons (saved by Fritzing 0.9.5d)
circuit board: 13.827cm x 14.1738cm
breadboards: 1

parts:
  Onderdeel1 = LED Tactile Button 12mm [part_number=BOB-10467]
  Onderdeel2 = LED Tactile Button 12mm [part_number=BOB-10467]
  Onderdeel3 = LED Tactile Button 12mm [part_number=BOB-10467]
  Onderdeel4 = LED Tactile Button 12mm [part_number=BOB-10467]
  Onderdeel5 = LED Tactile Button 12mm [part_number=BOB-10467]
  Onderdeel6 = LED Tactile Button 12mm [part_number=BOB-10467]
  R1 = Resistor [tolerance=±5% resistance=220 package=THT]
  IC1 = IC, DIP package, 24 pins [chip_label=IC]
  Onderdeel7 = LED Tactile Button 12mm [part_number=BOB-10467]
  Onderdeel8 = LED Tactile Button 12mm [part_number=BOB-10467]
  Onderdeel9 = LED Tactile Button 12mm [part_number=BOB-10467]
  Onderdeel10 = LED Tactile Button 12mm [part_number=BOB-10467]
  Onderdeel11 = LED Tactile Button 12mm [part_number=BOB-10467]
  Onderdeel12 = LED Tactile Button 12mm [part_number=BOB-10467]
  Onderdeel13 = LED Tactile Button 12mm [part_number=BOB-10467]
  Onderdeel14 = LED Tactile Button 12mm [part_number=BOB-10467]
  Onderdeel15 = LED Tactile Button 12mm [part_number=BOB-10467]
  Onderdeel16 = LED Tactile Button 12mm [part_number=BOB-10467]
  Onderdeel17 = LED Tactile Button 12mm [part_number=BOB-10467]
  Onderdeel18 = LED Tactile Button 12mm [part_number=BOB-10467]
  Onderdeel19 = LED Tactile Button 12mm [part_number=BOB-10467]
  Onderdeel20 = LED Tactile Button 12mm [part_number=BOB-10467]
  Onderdeel21 = LED Tactile Button 12mm [part_number=BOB-10467]
  Onderdeel22 = LED Tactile Button 12mm [part_number=BOB-10467]
  Onderdeel23 = LED Tactile Button 12mm [part_number=BOB-10467]
  Onderdeel24 = LED Tactile Button 12mm [part_number=BOB-10467]
  Onderdeel25 = LED Tactile Button 12mm [part_number=BOB-10467]
  Onderdeel26 = LED Tactile Button 12mm [part_number=BOB-10467]
  Onderdeel27 = LED Tactile Button 12mm [part_number=BOB-10467]
  Onderdeel28 = LED Tactile Button 12mm [part_number=BOB-10467]
  Onderdeel29 = LED Tactile Button 12mm [part_number=BOB-10467]
  Onderdeel30 = LED Tactile Button 12mm [part_number=BOB-10467]
  Onderdeel31 = LED Tactile Button 12mm [part_number=BOB-10467]
  Onderdeel32 = LED Tactile Button 12mm [part_number=BOB-10467]
  R2 = Resistor [tolerance=±5% resistance=220 package=THT]
  R3 = Resistor [tolerance=±5% resistance=220 package=THT]
  R4 = Resistor [tolerance=±5% resistance=220 package=THT]
  R5 = Resistor [tolerance=±5% resistance=220 package=THT]
  R6 = Resistor [tolerance=±5% resistance=220 package=THT]
  R7 = Resistor [tolerance=±5% resistance=220 package=THT]
  R8 = Resistor [tolerance=±5% resistance=220 package=THT]
  R9 = Resistor [tolerance=±5% resistance=220 package=THT]
  R10 = Resistor [tolerance=±5% resistance=220 package=THT]
  R11 = Resistor [tolerance=±5% resistance=220 package=THT]
  R12 = Resistor [tolerance=±5% resistance=220 package=THT]
  R13 = Resistor [tolerance=±5% resistance=220 package=THT]
  R14 = Resistor [tolerance=±5% resistance=220 package=THT]
  R15 = Resistor [tolerance=±5% resistance=220 package=THT]
  R16 = Resistor [tolerance=±5% resistance=220 package=THT]
  R17 = Resistor [tolerance=±5% resistance=220 package=THT]
  R18 = Resistor [tolerance=±5% resistance=220 package=THT]
  R19 = Resistor [tolerance=±5% resistance=220 package=THT]

nets:
  N1: Onderdeel1.pin_1, Onderdeel2.pin_1, Onderdeel3.pin_1, Onderdeel4.pin_1, Onderdeel5.pin_1, Onderdeel6.pin_1, IC1.pin2
  N2: Onderdeel1.pin_2, IC1.pin21
  N3: Onderdeel1.pin_3, Onderdeel1.pin_5, Onderdeel2.pin_3, Onderdeel2.pin_5, Onderdeel3.pin_3, Onderdeel3.pin_5, Onderdeel4.pin_3, Onderdeel4.pin_5, Onderdeel5.pin_3, Onderdeel5.pin_5, Onderdeel6.pin_3, Onderdeel6.pin_5, Onderdeel7.pin_4, Onderdeel7.pin_6, Onderdeel8.pin_4, Onderdeel8.pin_6, Onderdeel9.pin_4, Onderdeel9.pin_6, Onderdeel10.pin_4, Onderdeel10.pin_6, Onderdeel11.pin_6
  N4: Onderdeel1.pin_4, Onderdeel1.pin_6, R5.Pin_1
  N5: Onderdeel2.pin_2, IC1.pin22
  N6: Onderdeel2.pin_4, Onderdeel2.pin_6, R4.Pin_1, R5.Pin_0
  N7: Onderdeel3.pin_2, IC1.pin23
  N8: Onderdeel3.pin_4, Onderdeel3.pin_6, R1.Pin_0, R4.Pin_0
  N9: Onderdeel4.pin_2, IC1.pin14
  N10: Onderdeel4.pin_4, Onderdeel4.pin_6, R1.Pin_1, R3.Pin_1
  N11: Onderdeel5.pin_2, IC1.pin15
  N12: Onderdeel5.pin_4, Onderdeel5.pin_6, R2.Pin_1, R3.Pin_0
  N13: Onderdeel6.pin_2, IC1.pin16
  N14: Onderdeel6.pin_4, Onderdeel6.pin_6, R2.Pin_0
  N15: Onderdeel7.pin_2, Onderdeel8.pin_2, Onderdeel10.pin_2, Onderdeel11.pin_2
  N16: Onderdeel12.pin_1, Onderdeel13.pin_1, Onderdeel14.pin_1, Onderdeel15.pin_1, Onderdeel16.pin_1, Onderdeel17.pin_1
  N17: Onderdeel12.pin_2, Onderdeel22.pin_2
  N18: Onderdeel12.pin_3, Onderdeel12.pin_5, Onderdeel13.pin_3, Onderdeel14.pin_3, Onderdeel14.pin_5, Onderdeel15.pin_3, Onderdeel15.pin_5, Onderdeel16.pin_3, Onderdeel16.pin_5, Onderdeel17.pin_3, Onderdeel17.pin_5, Onderdeel18.pin_3, Onderdeel18.pin_5, Onderdeel19.pin_3, Onderdeel19.pin_5, Onderdeel20.pin_3, Onderdeel20.pin_5, Onderdeel21.pin_3, Onderdeel21.pin_5, Onderdeel22.pin_3, Onderdeel23.pin_3, Onderdeel24.pin_3, Onderdeel24.pin_5, Onderdeel25.pin_3, Onderdeel25.pin_5, Onderdeel26.pin_3, Onderdeel26.pin_5
  N19: Onderdeel12.pin_4, Onderdeel12.pin_6, R6.Pin_1, R7.Pin_0
  N20: Onderdeel13.pin_4, Onderdeel13.pin_6, R6.Pin_0
  N21: Onderdeel14.pin_4, Onderdeel14.pin_6, R9.Pin_1, R10.Pin_0
  N22: Onderdeel15.pin_4, Onderdeel15.pin_6, R8.Pin_1, R9.Pin_0
  N23: Onderdeel16.pin_4, Onderdeel16.pin_6, R7.Pin_1, R8.Pin_0
  N24: Onderdeel17.pin_2, Onderdeel21.pin_2, Onderdeel24.pin_2, Onderdeel29.pin_2, Onderdeel31.pin_2, Onderdeel32.pin_2
  N25: Onderdeel17.pin_4, Onderdeel17.pin_6, R10.Pin_1
  N26: Onderdeel18.pin_1, Onderdeel19.pin_1, Onderdeel20.pin_1, Onderdeel21.pin_1, Onderdeel22.pin_1
  N27: Onderdeel18.pin_4, Onderdeel18.pin_6, R12.Pin_1, R13.Pin_0
  N28: Onderdeel19.pin_2, Onderdeel26.pin_2, Onderdeel28.pin_2, Onderdeel30.pin_2
  N29: Onderdeel19.pin_4, Onderdeel19.pin_6, R13.Pin_1, R14.Pin_0
  N30: Onderdeel20.pin_2, Onderdeel23.pin_2
  N31: Onderdeel20.pin_4, Onderdeel20.pin_6, R11.Pin_1, R12.Pin_0
  N32: Onderdeel21.pin_4, Onderdeel21.pin_6, R14.Pin_1
  N33: Onderdeel22.pin_4, Onderdeel22.pin_6, R11.Pin_0
  N34: Onderdeel23.pin_1, Onderdeel24.pin_1, Onderdeel25.pin_1, Onderdeel26.pin_1
  N35: Onderdeel23.pin_4, Onderdeel23.pin_6, R15.Pin_0
  N36: Onderdeel24.pin_4, Onderdeel24.pin_6, R17.Pin_1
  N37: Onderdeel25.pin_4, Onderdeel25.pin_6, R15.Pin_1, R16.Pin_0
  N38: Onderdeel26.pin_4, Onderdeel26.pin_6, R16.Pin_1, R17.Pin_0
  N39: Onderdeel27.pin_1, Onderdeel28.pin_1, Onderdeel29.pin_1, Onderdeel30.pin_1, Onderdeel31.pin_1, Onderdeel32.pin_1
  N40: Onderdeel27.pin_3, Onderdeel28.pin_3, Onderdeel28.pin_5, Onderdeel29.pin_3, Onderdeel29.pin_5, Onderdeel30.pin_3, Onderdeel31.pin_3, Onderdeel31.pin_5, Onderdeel32.pin_3
  N41: Onderdeel27.pin_4, Onderdeel27.pin_6, R18.Pin_0
  N42: Onderdeel28.pin_4, Onderdeel28.pin_6, R18.Pin_1, R19.Pin_0
  N43: Onderdeel29.pin_4, Onderdeel29.pin_6, R19.Pin_1

custom parts:
  LED Tactile Button 12mm: A LED tactile switch
