# Fritzing sketch Analog button selector (saved by Fritzing 0.9.5d)
circuit board: 8.46667cm x 5.64444cm
breadboards: 1

parts:
  SW1 = LED Tactile Button 12mm
  SW2 = LED Tactile Button 12mm
  R1 = Resistor [tolerance=±5% resistance=4.7k package=THT]
  R2 = Resistor [tolerance=±5% resistance=470 package=THT]
  Analog_in = female pin header, 1 pin [form="♀ (female)"]
  GND = female pin header, 1 pin [form="♀ (female)"]
  Vdd = female pin header, 1 pin [form="♀ (female)"]

nets:
  N1: SW1.pin_3, SW1.pin_5, SW2.pin_3, SW2.pin_5, Analog_in.pin1
  N2: SW1.pin_4, SW1.pin_6, R1.Pin_1, R2.Pin_0
  N3: SW2.pin_4, SW2.pin_6, R2.Pin_1, Vdd.pin1
  N4: R1.Pin_0, GND.pin1

notes:
  SW1 levert Vdd / 2: R1/(R1+R2)
  SW2 levert Vdd: (R1+R2)/(R1+R2)

custom parts:
  LED Tactile Button 12mm: A LED tactile switch
