# Fritzing sketch Components (saved by Fritzing 0.9.5d)
breadboards: 1

parts:
  Teensy1 = Teensy 4.0
  IC1 = Voltage Regulator [package=78xxl]
  D1 = Schottky Diode [part_number=1N5817 package="300 mil [THT]"]
  D2 = Schottky Diode [part_number=1N5817 package="300 mil [THT]"]
  TCA9548A = IC, DIP package, 24 pins [chip_label=IC]
  R1 = Resistor [tolerance=±5% resistance=10k package=THT]
  OLED1 = OLED 128x64 I2C Monochrome Display
  MCP23017_A = IC, DIP package, 28 pins [chip_label=IC]
  MCP23017_B = IC, DIP package, 28 pins [chip_label=IC]
  Rotary_Encoder = Rotary Encoder [package=THT]
  MAX7219CNG = IC, DIP package, 24 pins [chip_label=IC]
  74HCT125 = IC, DIP package, 14 pins [chip_label=IC]
  R2 = Resistor [tolerance=±5% resistance=10k package=THT]
  LS1 = LED Tactile Button 12mm [part_number="LED Switch"]
  R3 = Resistor [tolerance=±5% resistance=2.2k package=THT]
  LS2 = LED Tactile Button 12mm [part_number="LED Switch"]
  R4 = Resistor [tolerance=±5% resistance=2.2k package=THT]
  LS3 = LED Tactile Button 12mm [part_number="LED Switch"]
  R5 = Resistor [tolerance=±5% resistance=2.2k package=THT]
  LS4 = LED Tactile Button 12mm [part_number="LED Switch"]
  LS5 = LED Tactile Button 12mm [part_number="LED Switch"]
  R6 = Resistor [tolerance=±5% resistance=2.2k package=THT]
  R7 = Resistor [tolerance=±5% resistance=2.2k package=THT]
  LS6 = LED Tactile Button 12mm [part_number="LED Switch"]
  R8 = Resistor [tolerance=±5% resistance=2.2k package=THT]

nets:
  GND: Teensy1.pin_1, Teensy1.pin_17, Teensy1.pin_32, IC1.GND, TCA9548A.pin2, R1.Pin_0, OLED1.GND, MCP23017_A.pin10, MCP23017_A.pin15, MCP23017_A.pin16, MCP23017_A.pin17, MCP23017_B.pin10, MCP23017_B.pin15, MCP23017_B.pin16, Rotary_Encoder.EncoderPinC, Rotary_Encoder.SwitchrPinD, MAX7219CNG.pin4, MAX7219CNG.pin9, 74HCT125.pin1, 74HCT125.pin4, 74HCT125.pin7, 74HCT125.pin10, R3.Pin_0
  fromXFM2: Teensy1.pin_2
  toXFM2: Teensy1.pin_3
  INT-A: Teensy1.pin_4, MCP23017_A.pin20
  INT-B: Teensy1.pin_5, MCP23017_B.pin20
  CS: Teensy1.pin_12, 74HCT125.pin2
  MOSI: Teensy1.pin_13, 74HCT125.pin5
  N1: Teensy1.pin_14, R1.Pin_1
  SCK: Teensy1.pin_20, 74HCT125.pin9
  Btn-P6: Teensy1.pin_23
  Btn-P5: Teensy1.pin_24
  I2C-SDA: Teensy1.pin_25, TCA9548A.pin3, MCP23017_A.pin13, MCP23017_B.pin13
  I2C-SCL: Teensy1.pin_26, TCA9548A.pin4, MCP23017_A.pin12, MCP23017_B.pin12
  Btn-P4: Teensy1.pin_27
  Btn-P3: Teensy1.pin_28
  Btn-P2: Teensy1.pin_29
  Btn-P1: Teensy1.pin_30, LS1.pin_4, LS2.pin_4, LS3.pin_4, LS4.pin_4, LS5.pin_4, LS6.pin_4
  3.3V: Teensy1.pin_31, TCA9548A.pin1, OLED1.VDD, MCP23017_A.pin9, MCP23017_A.pin18, MCP23017_B.pin9, MCP23017_B.pin17, MCP23017_B.pin18, LS6.pin_3, R8.Pin_0
  Vteensy: Teensy1.pin33, D1.cathode
  9V: IC1.IN
  5V: IC1.OUT, D1.anode, D2.anode, MAX7219CNG.pin19, 74HCT125.pin14, R2.Pin_1
  Vxfm2: D2.cathode
  SD0: TCA9548A.pin9, OLED1.SDA
  SC0: TCA9548A.pin10, OLED1.SCK
  SD1: TCA9548A.pin11
  SC1: TCA9548A.pin12
  SD2: TCA9548A.pin13
  SC2: TCA9548A.pin14
  SD3: TCA9548A.pin15
  SC3: TCA9548A.pin16
  SD4: TCA9548A.pin17
  SC4: TCA9548A.pin18
  SD5: TCA9548A.pin19
  SC5: TCA9548A.pin20
  SD6: TCA9548A.pin21
  SC6: TCA9548A.pin22
  EncA-1: MCP23017_A.pin1, Rotary_Encoder.EncoderPinA
  EncB-1: MCP23017_A.pin2, Rotary_Encoder.EncoderPinB
  EncS-1: MCP23017_A.pin3, Rotary_Encoder.SwitchPinE
  EncA-2: MCP23017_A.pin4
  EncB-2: MCP23017_A.pin5
  EncS-2: MCP23017_A.pin6
  EncA-5: MCP23017_A.pin7
  EncB-5: MCP23017_A.pin8
  EncA-3: MCP23017_A.pin21
  EncB-3: MCP23017_A.pin22
  EncS-3: MCP23017_A.pin23
  EncA-4: MCP23017_A.pin24
  EncB-4: MCP23017_A.pin25
  EncS-4: MCP23017_A.pin26
  EncS-5: MCP23017_A.pin28
  EncA-6: MCP23017_B.pin1
  EncB-6: MCP23017_B.pin2
  EncS-6: MCP23017_B.pin3
  EncA-7: MCP23017_B.pin4
  EncB-7: MCP23017_B.pin5
  EncS-7: MCP23017_B.pin6
  EncA-10: MCP23017_B.pin7
  EncB-10: MCP23017_B.pin8
  EncA-8: MCP23017_B.pin21
  EncB-8: MCP23017_B.pin22
  EncS-8: MCP23017_B.pin23
  EncA-9: MCP23017_B.pin24
  EncB-9: MCP23017_B.pin25
  EncS-9: MCP23017_B.pin26
  EncS-10: MCP23017_B.pin28
  DIN: MAX7219CNG.pin1, 74HCT125.pin6
  DIG0: MAX7219CNG.pin2, LS1.pin_2, LS2.pin_2, LS3.pin_2, LS4.pin_2, LS5.pin_2, LS6.pin_2
  DIG4: MAX7219CNG.pin3
  DIG6: MAX7219CNG.pin5
  DIG2: MAX7219CNG.pin6
  DIG3: MAX7219CNG.pin7
  DIG7: MAX7219CNG.pin8
  DIG5: MAX7219CNG.pin10
  DIG1: MAX7219CNG.pin11
  LOAD: MAX7219CNG.pin12, 74HCT125.pin3
  CLK: MAX7219CNG.pin13, 74HCT125.pin8
  SEGA: MAX7219CNG.pin14, LS1.pin_1
  SEGF: MAX7219CNG.pin15, LS6.pin_1
  SEGB: MAX7219CNG.pin16, LS3.pin_1
  SEGG: MAX7219CNG.pin17, LS2.pin_1
  N2: MAX7219CNG.pin18, R2.Pin_0
  SEGC: MAX7219CNG.pin20, LS4.pin_1
  SEGE: MAX7219CNG.pin21, LS5.pin_1
  N3: LS1.pin_3, LS1.pin_5, R3.Pin_1, R4.Pin_1
  N4: LS2.pin_3, R4.Pin_0, R5.Pin_1
  N5: LS3.pin_3, R5.Pin_0, R6.Pin_1
  N6: LS4.pin_3, R6.Pin_0, R7.Pin_1
  N7: LS5.pin_3, R7.Pin_0, R8.Pin_1

notes:
  MISO is not used: is a pull down resistor needed?
  Six more OLEd's (at SCn/SDn)
  Nine more encoders (EncA-n/EncB-n/EncS-n)
  Five more rows (Rn) and Seven more segments (SEGn)

custom parts:
  Teensy 4.0: The Teensy is a complete USB-based microcontoller development system, in a very small footprint, capable of implementing many types of projects. All programming is done via the USB port. No special programmer is needed, only a standard micro-USB cable and a PC or Macintosh with a USB port.
  Rotary Encoder: Rotary Encoder from ALPSec11e with switch.
  LED Tactile Button 12mm: A LED tactile switch
