# Fritzing sketch MCP23017s (saved by Fritzing 0.9.5d)
circuit board: 5cm x 4cm
breadboards: 1

parts:
  IC1 = IC, DIP package, 28 pins [chip_label=IC]
  IC2 = IC, DIP package, 28 pins [chip_label=IC]
  J2 = female pin header, 8 pins [form="♀ (female)"]
  J3 = female pin header, 8 pins [form="♀ (female)"]
  J4 = female pin header, 8 pins [form="♀ (female)"]
  J6 = female pin header, 6 pins [form="♀ (female)"]
  J1 = female pin header, 10 pins [form="♀ (female)"]

nets:
  N1: IC1.pin1, J1.pin1
  N2: IC1.pin2, J1.pin2
  N3: IC1.pin3, J1.pin3
  N4: IC1.pin4, J1.pin4
  N5: IC1.pin5, J1.pin5
  N6: IC1.pin6, J1.pin6
  N7: IC1.pin7, J1.pin7
  N8: IC1.pin8, J1.pin8
  3.3V: IC1.pin9, IC1.pin17, IC1.pin18, IC2.pin9, IC2.pin18, J6.pin3
  GND: IC1.pin10, IC1.pin15, IC1.pin16, IC2.pin10, IC2.pin15, IC2.pin16, IC2.pin17, J6.pin4, J1.pin9, J1.pin10
  I2C-SCL: IC1.pin12, IC2.pin12, J6.pin5
  I2C-SDA: IC1.pin13, IC2.pin13, J6.pin6
  INT-B: IC1.pin20, J6.pin2
  N9: IC1.pin21, J2.pin8
  N10: IC1.pin22, J2.pin7
  N11: IC1.pin23, J2.pin6
  N12: IC1.pin24, J2.pin5
  N13: IC1.pin25, J2.pin4
  N14: IC1.pin26, J2.pin3
  N15: IC1.pin27, J2.pin2
  N16: IC1.pin28, J2.pin1
  N17: IC2.pin1, J3.pin1
  N18: IC2.pin2, J3.pin2
  N19: IC2.pin3, J3.pin3
  N20: IC2.pin4, J3.pin4
  N21: IC2.pin5, J3.pin5
  N22: IC2.pin6, J3.pin6
  N23: IC2.pin7, J3.pin7
  N24: IC2.pin8, J3.pin8
  INT-A: IC2.pin20, J6.pin1
  N25: IC2.pin21, J4.pin8
  N26: IC2.pin22, J4.pin7
  N27: IC2.pin23, J4.pin6
  N28: IC2.pin24, J4.pin5
  N29: IC2.pin25, J4.pin4
  N30: IC2.pin26, J4.pin3
  N31: IC2.pin27, J4.pin2
  N32: IC2.pin28, J4.pin1

notes:
  I2C address = 0x20
  I2C address = 0x24
