# Fritzing sketch TCA9548A-OLEDs (saved by Fritzing 0.9.5d)
circuit board: 5.52022cm x 8cm
circuit board: 5cm x 7cm
breadboards: 2

parts:
  OLED6 = OLED 128x64 I2C Monochrome Display
  OLED5 = OLED 128x64 I2C Monochrome Display
  OLED2 = OLED 128x64 I2C Monochrome Display
  OLED1 = OLED 128x64 I2C Monochrome Display
  OLED0 = OLED 128x64 I2C Monochrome Display
  J3 = female pin header, 8 pins [form="♀ (female)"]
  TCA9548A = Adafruit TCA9548A
  OLED4 = OLED 128x64 I2C Monochrome Display
  OLED3 = OLED 128x64 I2C Monochrome Display
  J4 = female pin header, 8 pins [form="♀ (female)"]
  J5 = female pin header, 4 pins [form="♀ (female)"]
  J7 = female pin header, 18 pins [form="♀ (female)"]  # not connected
  J6 = female pin header, 24 pins [form="♀ (female)"]  # not connected

nets:
  GND: OLED6.GND, OLED5.GND, OLED2.GND, OLED1.GND, OLED0.GND, J3.pin5, TCA9548A.GND, OLED4.GND, OLED3.GND, J4.pin1, J5.pin2
  Vcc: OLED6.VDD, OLED5.VDD, OLED2.VDD, OLED1.VDD, OLED0.VDD, J3.pin6, TCA9548A.VCC, OLED4.VDD, OLED3.VDD, J4.pin2, J5.pin1
  SCL6: OLED6.SCK, J3.pin3, TCA9548A.6SCL, J4.pin5
  SDA6: OLED6.SDA, J3.pin4, TCA9548A.6SDA, J4.pin6
  SCL5: OLED5.SCK, J3.pin7, TCA9548A.5SCL, J4.pin7
  SDA5: OLED5.SDA, J3.pin8, TCA9548A.5SDA, J4.pin8
  SCL2: OLED2.SCK, TCA9548A.2SCL
  SDA2: OLED2.SDA, TCA9548A.2SDA
  SCL1: OLED1.SCK, TCA9548A.1SCL
  SDA1: OLED1.SDA, TCA9548A.1SDA
  SCL0: OLED0.SCK, TCA9548A.0SCL
  SDA0: OLED0.SDA, TCA9548A.0SDA
  SDA7: J3.pin1, TCA9548A.7SDA, OLED3.SDA, J4.pin4
  SCL7: J3.pin2, TCA9548A.7SCL, OLED3.SCK, J4.pin3
  SDA4: TCA9548A.4SDA, OLED4.SDA
  SCL4: TCA9548A.4SCL, OLED4.SCK
  SDA-IN: TCA9548A.INPUTSDA, J5.pin3
  SCL-IN: TCA9548A.INPUTSCL, J5.pin4

custom parts:
  Adafruit TCA9548A: You just found the perfect I2C sensor, and you want to wire up two or three or more of them to your Arduino when you realize "Uh oh, this chip has a fixed I2C address, and from what I know about I2C, you cannot have two devices with the same address on the same SDA/SCL pins!" Are you out of luck? You would be, if you didn't have this ultra-cool TCA9548A 1-to-8 I2C multiplexer! Finally, a way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
