# Fritzing sketch Teensy (saved by Fritzing 0.9.5d)
circuit board: 7cm x 5cm
breadboards: 1

parts:
  Teensy = Teensy 4.0
  Panel1 = female pin header, 6 pins [form="♀ (female)"]
  Panel2 = female pin header, 2 pins [form="♀ (female)"]
  Panel3 = female pin header, 2 pins [form="♀ (female)"]
  Panel4 = female pin header, 2 pins [form="♀ (female)"]
  Panel5 = female pin header, 2 pins [form="♀ (female)"]
  Panel6 = female pin header, 2 pins [form="♀ (female)"]
  TCA9548A = female pin header, 4 pins [form="♀ (female)"]
  MCP23017s = female pin header, 6 pins [form="♀ (female)"]
  Power = female pin header, 2 pins [form="♀ (female)"]
  XFM2 = female pin header, 2 pins [form="♀ (female)"]
  R1 = Resistor [tolerance=±5% resistance=10k package=THT]
  R2 = Resistor [tolerance=±5% resistance=10k package=THT]

nets:
  GND: Teensy.pin_1, Teensy.pin_17, Teensy.pin_32, Panel1.pin2, Panel2.pin2, Panel3.pin2, Panel4.pin2, Panel5.pin2, Panel6.pin2, TCA9548A.pin3, MCP23017s.pin4, Power.pin2
  fromXFM2: Teensy.pin_2, XFM2.pin1
  toXFM2: Teensy.pin_3, XFM2.pin2
  INT-A: Teensy.pin_4, MCP23017s.pin1
  INT-B: Teensy.pin_5, MCP23017s.pin2
  CS: Teensy.pin_12, Panel1.pin5
  MOSI: Teensy.pin_13, Panel1.pin4
  3.3V: Teensy.pin_16, Teensy.pin_31, Panel1.pin6, TCA9548A.pin4, MCP23017s.pin3, R1.Pin_1, R2.Pin_1
  SCK: Teensy.pin_20, Panel1.pin3
  Btn-P6: Teensy.pin_23, Panel6.pin1
  Btn-P5: Teensy.pin_24, Panel5.pin1
  I2C-SDA: Teensy.pin_25, TCA9548A.pin2, MCP23017s.pin6, R2.Pin_0
  I2C-SCL: Teensy.pin_26, TCA9548A.pin1, MCP23017s.pin5, R1.Pin_0
  Btn-P4: Teensy.pin_27, Panel4.pin1
  Btn-P3: Teensy.pin_28, Panel3.pin1
  Btn-P2: Teensy.pin_29, Panel2.pin1
  Btn-P1: Teensy.pin_30, Panel1.pin1
  Vteensy: Teensy.pin33, Power.pin1

custom parts:
  Teensy 4.0: The Teensy is a complete USB-based microcontoller development system, in a very small footprint, capable of implementing many types of projects. All programming is done via the USB port. No special programmer is needed, only a standard micro-USB cable and a PC or Macintosh with a USB port.
