# Fritzing sketch buttons-blue-ic (saved by Fritzing 0.9.5d)
circuit board: 4.99147cm x 12.9558cm
breadboards: 1

parts:
  Switch_P1-1 = LED Tactile Button 12mm
  Switch_P1-2 = LED Tactile Button 12mm
  Switch_P1-3 = LED Tactile Button 12mm
  Switch_P1-4 = LED Tactile Button 12mm
  Switch_P1-5 = LED Tactile Button 12mm
  R2 = Resistor [tolerance=±5% resistance=220 package=THT]
  R3 = Resistor [tolerance=±5% resistance=220 package=THT]
  R4 = Resistor [tolerance=±5% resistance=220 package=THT]
  R5 = Resistor [tolerance=±5% resistance=220 package=THT]
  R6 = Resistor [tolerance=±5% resistance=220 package=THT]
  P4 = female pin header, 8 pins [form="♀ (female)"]
  P3 = female pin header, 8 pins [form="♀ (female)"]
  P5 = female pin header, 8 pins [form="♀ (female)"]
  P6 = female pin header, 8 pins [form="♀ (female)"]
  R7 = Resistor [tolerance=±5% resistance=10k package=THT]
  to_Power = female pin header, 2 pins [form="♀ (female)"]
  R8 = Resistor [tolerance=±5% resistance=220 package=THT]
  to_Teensy = female pin header, 6 pins [form="♀ (female)"]
  MAX7219CNG = IC, DIP package, 24 pins [chip_label=IC]
  74HCT125 = IC, DIP package, 14 pins [chip_label=IC]
  P2 = female pin header, 8 pins [form="♀ (female)"]
  C2 = Ceramic Capacitor [capacitance=100nF package="100 mil [THT, multilayer]"]
  C1 = Electrolytic Capacitor [capacitance=10µF package="100 mil [THT, electrolytic]"]
  R10 = TRIMPOT [part_number=20kΩ package=3362u-2]
  R11 = Resistor [tolerance=±5% resistance=100k package=THT]
  Switch_P1-6 = LED Tactile Button 12mm [part_number=BOB-10467]
  J1 = female pin header, 18 pins [form="♀ (female)"]  # not connected
  J2 = female pin header, 48 pins [form="♀ (female)"]  # not connected

nets:
  SEGE: Switch_P1-1.pin_1, P4.pin2, P3.pin2, P5.pin2, P6.pin2, MAX7219CNG.pin21, P2.pin2
  DIG0: Switch_P1-1.pin_2, Switch_P1-2.pin_2, Switch_P1-3.pin_2, Switch_P1-4.pin_2, Switch_P1-5.pin_2, MAX7219CNG.pin2, Switch_P1-6.pin_2
  Btn-P1: Switch_P1-1.pin_3, Switch_P1-1.pin_5, Switch_P1-2.pin_3, Switch_P1-2.pin_5, Switch_P1-3.pin_3, Switch_P1-3.pin_5, Switch_P1-4.pin_3, Switch_P1-4.pin_5, Switch_P1-5.pin_3, Switch_P1-5.pin_5, to_Teensy.pin1, R11.Pin_0, Switch_P1-6.pin_3, Switch_P1-6.pin_5
  N1: Switch_P1-1.pin_4, Switch_P1-1.pin_6, R5.Pin_1, R8.Pin_0
  SEGG: Switch_P1-2.pin_1, P4.pin3, P3.pin3, P5.pin3, P6.pin3, MAX7219CNG.pin17, P2.pin3
  N2: Switch_P1-2.pin_4, Switch_P1-2.pin_6, R4.Pin_1, R5.Pin_0
  SEGC: Switch_P1-3.pin_1, P4.pin4, P3.pin4, P5.pin4, P6.pin4, MAX7219CNG.pin20, P2.pin4
  N3: Switch_P1-3.pin_4, Switch_P1-3.pin_6, R4.Pin_0, R6.Pin_1
  SEGB: Switch_P1-4.pin_1, P3.pin8, P5.pin8, MAX7219CNG.pin16, P2.pin8
  N4: Switch_P1-4.pin_4, Switch_P1-4.pin_6, R3.Pin_1, R6.Pin_0
  SEGA: Switch_P1-5.pin_1, P4.pin6, P3.pin6, P5.pin6, P6.pin6, MAX7219CNG.pin14, P2.pin6
  N5: Switch_P1-5.pin_4, Switch_P1-5.pin_6, R2.Pin_1, R3.Pin_0
  3.3V: R2.Pin_0, P4.pin5, P3.pin5, P5.pin5, P6.pin5, to_Teensy.pin6, P2.pin5, Switch_P1-6.pin_4, Switch_P1-6.pin_6
  DIG3: P4.pin1, MAX7219CNG.pin7
  SEGF: P4.pin7, P3.pin7, P5.pin7, P6.pin7, MAX7219CNG.pin15, P2.pin7, Switch_P1-6.pin_1
  DIG6: P4.pin8, MAX7219CNG.pin5
  DIG2: P3.pin1, MAX7219CNG.pin6
  DIG4: P5.pin1, MAX7219CNG.pin3
  DIG5: P6.pin1, MAX7219CNG.pin10
  DIG7: P6.pin8, MAX7219CNG.pin8
  N6: R7.Pin_0, MAX7219CNG.pin18
  N7: R7.Pin_1, R10.CCW
  GND: to_Power.pin1, MAX7219CNG.pin4, MAX7219CNG.pin9, 74HCT125.pin1, 74HCT125.pin4, 74HCT125.pin7, 74HCT125.pin10, C2.1, C1.-
  5V: to_Power.pin2, MAX7219CNG.pin19, 74HCT125.pin14, C2.0, C1.+, R10.WIPER
  GNDt: R8.Pin_1, to_Teensy.pin2, R11.Pin_1
  SCK: to_Teensy.pin3, 74HCT125.pin9
  MOSI: to_Teensy.pin4, 74HCT125.pin5
  CS: to_Teensy.pin5, 74HCT125.pin2
  DIN: MAX7219CNG.pin1, 74HCT125.pin6
  DIG1: MAX7219CNG.pin11, P2.pin1
  LOAD: MAX7219CNG.pin12, 74HCT125.pin3
  CLK: MAX7219CNG.pin13, 74HCT125.pin8

custom parts:
  LED Tactile Button 12mm: A LED tactile switch
