# Fritzing sketch front-panel (saved by Fritzing 0.9.5d)
perfboards: 9

parts:
  Onderdeel1 = LED Tactile Button 12mm [part_number=BOB-10467]
  Onderdeel2 = LED Tactile Button 12mm [part_number=BOB-10467]
  Onderdeel3 = LED Tactile Button 12mm [part_number=BOB-10467]
  Onderdeel4 = LED Tactile Button 12mm [part_number=BOB-10467]
  Onderdeel5 = LED Tactile Button 12mm [part_number=BOB-10467]
  Onderdeel6 = LED Tactile Button 12mm [part_number=BOB-10467]
  Onderdeel7 = LED Tactile Button 12mm [part_number=BOB-10467]
  Onderdeel8 = LED Tactile Button 12mm [part_number=BOB-10467]
  Onderdeel9 = LED Tactile Button 12mm [part_number=BOB-10467]
  Onderdeel10 = LED Tactile Button 12mm [part_number=BOB-10467]
  Onderdeel11 = LED Tactile Button 12mm [part_number=BOB-10467]
  Onderdeel12 = LED Tactile Button 12mm [part_number=BOB-10467]
  Onderdeel13 = LED Tactile Button 12mm [part_number=BOB-10467]
  Onderdeel14 = LED Tactile Button 12mm [part_number=BOB-10467]
  Onderdeel15 = LED Tactile Button 12mm [part_number=BOB-10467]
  Onderdeel16 = LED Tactile Button 12mm [part_number=BOB-10467]
  Onderdeel17 = LED Tactile Button 12mm [part_number=BOB-10467]
  Onderdeel18 = LED Tactile Button 12mm [part_number=BOB-10467]
  Onderdeel19 = LED Tactile Button 12mm [part_number=BOB-10467]
  Onderdeel20 = LED Tactile Button 12mm [part_number=BOB-10467]
  Onderdeel21 = LED Tactile Button 12mm [part_number=BOB-10467]
  Onderdeel22 = LED Tactile Button 12mm [part_number=BOB-10467]
  Onderdeel23 = LED Tactile Button 12mm [part_number=BOB-10467]
  Onderdeel24 = LED Tactile Button 12mm [part_number=BOB-10467]
  Onderdeel25 = LED Tactile Button 12mm [part_number=BOB-10467]
  Onderdeel26 = LED Tactile Button 12mm [part_number=BOB-10467]
  Onderdeel27 = LED Tactile Button 12mm [part_number=BOB-10467]
  Onderdeel28 = LED Tactile Button 12mm [part_number=BOB-10467]
  Onderdeel29 = LED Tactile Button 12mm [part_number=BOB-10467]
  Onderdeel30 = LED Tactile Button 12mm [part_number=BOB-10467]
  Onderdeel31 = LED Tactile Button 12mm [part_number=BOB-10467]
  Onderdeel32 = LED Tactile Button 12mm [part_number=BOB-10467]
  OLED1 = OLED 128x64 I2C Monochrome Display  # not connected
  OLED2 = OLED 128x64 I2C Monochrome Display  # not connected
  OLED3 = OLED 128x64 I2C Monochrome Display  # not connected
  OLED4 = OLED 128x64 I2C Monochrome Display  # not connected
  OLED5 = OLED 128x64 I2C Monochrome Display  # not connected
  OLED6 = OLED 128x64 I2C Monochrome Display  # not connected
  OLED7 = OLED 128x64 I2C Monochrome Display  # not connected
  RE1 = Rotary Encoder [package=THT]  # not connected
  RE2 = Rotary Encoder [package=THT]  # not connected
  RE3 = Rotary Encoder [package=THT]  # not connected
  RE4 = Rotary Encoder [package=THT]  # not connected
  RE5 = Rotary Encoder [package=THT]  # not connected
  RE6 = Rotary Encoder [package=THT]  # not connected
  Onderdeel33 = LED Tactile Button 12mm [part_number=BOB-10467]
  Onderdeel34 = LED Tactile Button 12mm [part_number=BOB-10467]
  Onderdeel35 = LED Tactile Button 12mm [part_number=BOB-10467]
  Onderdeel36 = LED Tactile Button 12mm [part_number=BOB-10467]
  Onderdeel37 = LED Tactile Button 12mm [part_number=BOB-10467]
  Onderdeel38 = LED Tactile Button 12mm [part_number=BOB-10467]
  Onderdeel39 = LED Tactile Button 12mm [part_number=BOB-10467]
  Onderdeel40 = LED Tactile Button 12mm [part_number=BOB-10467]
  Onderdeel41 = LED Tactile Button 12mm [part_number=BOB-10467]
  RE7 = Rotary Encoder [package=THT]  # not connected

nets:
  N1: Onderdeel1.pin_3, Onderdeel1.pin_5
  N2: Onderdeel1.pin_4, Onderdeel1.pin_6
  N3: Onderdeel2.pin_3, Onderdeel2.pin_5
  N4: Onderdeel2.pin_4, Onderdeel2.pin_6
  N5: Onderdeel3.pin_3, Onderdeel3.pin_5
  N6: Onderdeel3.pin_4, Onderdeel3.pin_6
  N7: Onderdeel4.pin_3, Onderdeel4.pin_5
  N8: Onderdeel4.pin_4, Onderdeel4.pin_6
  N9: Onderdeel5.pin_3, Onderdeel5.pin_5
  N10: Onderdeel5.pin_4, Onderdeel5.pin_6
  N11: Onderdeel6.pin_3, Onderdeel6.pin_5
  N12: Onderdeel6.pin_4, Onderdeel6.pin_6
  N13: Onderdeel7.pin_3, Onderdeel7.pin_5
  N14: Onderdeel7.pin_4, Onderdeel7.pin_6
  N15: Onderdeel8.pin_3, Onderdeel8.pin_5
  N16: Onderdeel8.pin_4, Onderdeel8.pin_6
  N17: Onderdeel9.pin_3, Onderdeel9.pin_5
  N18: Onderdeel9.pin_4, Onderdeel9.pin_6
  N19: Onderdeel10.pin_3, Onderdeel10.pin_5
  N20: Onderdeel10.pin_4, Onderdeel10.pin_6
  N21: Onderdeel11.pin_3, Onderdeel11.pin_5
  N22: Onderdeel11.pin_4, Onderdeel11.pin_6
  N23: Onderdeel12.pin_3, Onderdeel12.pin_5
  N24: Onderdeel12.pin_4, Onderdeel12.pin_6
  N25: Onderdeel13.pin_3, Onderdeel13.pin_5
  N26: Onderdeel13.pin_4, Onderdeel13.pin_6
  N27: Onderdeel14.pin_3, Onderdeel14.pin_5
  N28: Onderdeel14.pin_4, Onderdeel14.pin_6
  N29: Onderdeel15.pin_3, Onderdeel15.pin_5
  N30: Onderdeel15.pin_4, Onderdeel15.pin_6
  N31: Onderdeel16.pin_3, Onderdeel16.pin_5
  N32: Onderdeel16.pin_4, Onderdeel16.pin_6
  N33: Onderdeel17.pin_3, Onderdeel17.pin_5
  N34: Onderdeel17.pin_4, Onderdeel17.pin_6
  N35: Onderdeel18.pin_3, Onderdeel18.pin_5
  N36: Onderdeel18.pin_4, Onderdeel18.pin_6
  N37: Onderdeel19.pin_3, Onderdeel19.pin_5
  N38: Onderdeel19.pin_4, Onderdeel19.pin_6
  N39: Onderdeel20.pin_3, Onderdeel20.pin_5
  N40: Onderdeel20.pin_4, Onderdeel20.pin_6
  N41: Onderdeel21.pin_3, Onderdeel21.pin_5
  N42: Onderdeel21.pin_4, Onderdeel21.pin_6
  N43: Onderdeel22.pin_3, Onderdeel22.pin_5
  N44: Onderdeel22.pin_4, Onderdeel22.pin_6
  N45: Onderdeel23.pin_3, Onderdeel23.pin_5
  N46: Onderdeel23.pin_4, Onderdeel23.pin_6
  N47: Onderdeel24.pin_3, Onderdeel24.pin_5
  N48: Onderdeel24.pin_4, Onderdeel24.pin_6
  N49: Onderdeel25.pin_3, Onderdeel25.pin_5
  N50: Onderdeel25.pin_4, Onderdeel25.pin_6
  N51: Onderdeel26.pin_3, Onderdeel26.pin_5
  N52: Onderdeel26.pin_4, Onderdeel26.pin_6
  N53: Onderdeel27.pin_3, Onderdeel27.pin_5
  N54: Onderdeel27.pin_4, Onderdeel27.pin_6
  N55: Onderdeel28.pin_3, Onderdeel28.pin_5
  N56: Onderdeel28.pin_4, Onderdeel28.pin_6
  N57: Onderdeel29.pin_3, Onderdeel29.pin_5
  N58: Onderdeel29.pin_4, Onderdeel29.pin_6
  N59: Onderdeel30.pin_3, Onderdeel30.pin_5
  N60: Onderdeel30.pin_4, Onderdeel30.pin_6
  N61: Onderdeel31.pin_3, Onderdeel31.pin_5
  N62: Onderdeel31.pin_4, Onderdeel31.pin_6
  N63: Onderdeel32.pin_3, Onderdeel32.pin_5
  N64: Onderdeel32.pin_4, Onderdeel32.pin_6
  N65: Onderdeel33.pin_3, Onderdeel33.pin_5
  N66: Onderdeel33.pin_4, Onderdeel33.pin_6
  N67: Onderdeel34.pin_4, Onderdeel34.pin_6
  N68: Onderdeel35.pin_4, Onderdeel35.pin_6
  N69: Onderdeel36.pin_3, Onderdeel36.pin_5
  N70: Onderdeel36.pin_4, Onderdeel36.pin_6
  N71: Onderdeel37.pin_3, Onderdeel37.pin_5
  N72: Onderdeel38.pin_3, Onderdeel38.pin_5
  N73: Onderdeel39.pin_3, Onderdeel39.pin_5
  N74: Onderdeel40.pin_3, Onderdeel40.pin_5
  N75: Onderdeel41.pin_4, Onderdeel41.pin_6

custom parts:
  LED Tactile Button 12mm: A LED tactile switch
  Rotary Encoder: Rotary Encoder from ALPSec11e with switch.
