# Fritzing sketch panel3-4 (saved by Fritzing 0.9.5d)
circuit board: 11.7084cm x 6.19134cm
breadboards: 1

parts:
  Onderdeel1 = LED Tactile Button 12mm [part_number=BOB-10467]
  Onderdeel2 = LED Tactile Button 12mm [part_number=BOB-10467]
  Onderdeel3 = LED Tactile Button 12mm [part_number=BOB-10467]
  Onderdeel4 = LED Tactile Button 12mm [part_number=BOB-10467]
  Onderdeel5 = LED Tactile Button 12mm [part_number=BOB-10467]
  Onderdeel6 = LED Tactile Button 12mm [part_number=BOB-10467]
  Onderdeel7 = LED Tactile Button 12mm [part_number=BOB-10467]
  Onderdeel8 = LED Tactile Button 12mm [part_number=BOB-10467]
  Onderdeel9 = LED Tactile Button 12mm [part_number=BOB-10467]
  J1 = female pin header, 8 pins [form="♀ (female)"]
  R1 = Resistor [tolerance=±5% resistance=220 package=THT]
  R2 = Resistor [tolerance=±5% resistance=220 package=THT]
  R3 = Resistor [tolerance=±5% resistance=220 package=THT]
  R4 = Resistor [tolerance=±5% resistance=220 package=THT]
  R5 = Resistor [tolerance=±5% resistance=220 package=THT]
  R6 = Resistor [tolerance=±5% resistance=220 package=THT]
  R7 = Resistor [tolerance=±5% resistance=220 package=THT]
  R8 = Resistor [tolerance=±5% resistance=220 package=THT]
  R9 = Resistor [tolerance=±5% resistance=220 package=THT]
  J2 = female pin header, 2 pins [form="♀ (female)"]
  Onderdeel10 = LED Tactile Button 12mm [part_number=BOB-10467]
  Onderdeel11 = LED Tactile Button 12mm [part_number=BOB-10467]
  Onderdeel12 = LED Tactile Button 12mm [part_number=BOB-10467]
  Onderdeel13 = LED Tactile Button 12mm [part_number=BOB-10467]
  Onderdeel14 = LED Tactile Button 12mm [part_number=BOB-10467]
  Onderdeel15 = LED Tactile Button 12mm [part_number=BOB-10467]
  R10 = Resistor [tolerance=±5% resistance=220 package=THT]
  R11 = Resistor [tolerance=±5% resistance=220 package=THT]
  R12 = Resistor [tolerance=±5% resistance=220 package=THT]
  R13 = Resistor [tolerance=±5% resistance=220 package=THT]
  R14 = Resistor [tolerance=±5% resistance=220 package=THT]
  J4 = female pin header, 8 pins [form="♀ (female)"]
  J5 = female pin header, 2 pins [form="♀ (female)"]
  R15 = Resistor [tolerance=±5% resistance=220 package=THT]
  R16 = Resistor [tolerance=±5% resistance=100k package=THT]
  R17 = Resistor [tolerance=±5% resistance=100k package=THT]
  J6 = female pin header, 24 pins [form="♀ (female)"]  # not connected
  J7 = female pin header, 45 pins [form="♀ (female)"]  # not connected

nets:
  DIG6: Onderdeel1.pin_1, Onderdeel2.pin_1, Onderdeel3.pin_1, Onderdeel4.pin_1, Onderdeel5.pin_1, J1.pin8
  SEGG: Onderdeel1.pin_2, J1.pin3
  Btn-P4: Onderdeel1.pin_3, Onderdeel2.pin_3, Onderdeel2.pin_5, Onderdeel3.pin_3, Onderdeel3.pin_5, Onderdeel4.pin_3, Onderdeel4.pin_5, Onderdeel5.pin_3, Onderdeel5.pin_5, Onderdeel6.pin_3, Onderdeel6.pin_5, Onderdeel7.pin_3, Onderdeel7.pin_5, Onderdeel8.pin_3, Onderdeel8.pin_5, Onderdeel9.pin_3, Onderdeel9.pin_5, J2.pin2, R17.Pin_1
  N1: Onderdeel1.pin_4, R8.Pin_1, R9.Pin_1
  SEGE: Onderdeel2.pin_2, Onderdeel6.pin_2, J1.pin2
  N2: Onderdeel2.pin_4, Onderdeel2.pin_6, R7.Pin_1, R8.Pin_0
  SEGC: Onderdeel3.pin_2, Onderdeel7.pin_2, J1.pin4
  N3: Onderdeel3.pin_4, Onderdeel3.pin_6, R6.Pin_1, R7.Pin_0
  SEGF: Onderdeel4.pin_2, Onderdeel8.pin_2, J1.pin7
  N4: Onderdeel4.pin_4, Onderdeel4.pin_6, R5.Pin_1, R6.Pin_0
  SEGA: Onderdeel5.pin_2, Onderdeel9.pin_2, J1.pin6
  N5: Onderdeel5.pin_4, Onderdeel5.pin_6, R1.Pin_0, R5.Pin_0
  DIG3: Onderdeel6.pin_1, Onderdeel7.pin_1, Onderdeel8.pin_1, Onderdeel9.pin_1, J1.pin1
  3.3V: Onderdeel6.pin_4, Onderdeel6.pin_6, J1.pin5, R4.Pin_1
  N6: Onderdeel7.pin_4, Onderdeel7.pin_6, R2.Pin_1, R4.Pin_0
  N7: Onderdeel8.pin_4, Onderdeel8.pin_6, R2.Pin_0, R3.Pin_1
  N8: Onderdeel9.pin_4, Onderdeel9.pin_6, R1.Pin_1, R3.Pin_0
  GND: R9.Pin_0, J2.pin1, R17.Pin_0
  DIG2: Onderdeel10.pin_1, Onderdeel11.pin_1, Onderdeel12.pin_1, Onderdeel13.pin_1, Onderdeel14.pin_1, Onderdeel15.pin_1, J4.pin1
  SEGB-P3: Onderdeel10.pin_2, J4.pin8
  Btn-P3: Onderdeel10.pin_3, Onderdeel10.pin_5, Onderdeel11.pin_3, Onderdeel11.pin_5, Onderdeel12.pin_3, Onderdeel12.pin_5, Onderdeel13.pin_3, Onderdeel13.pin_5, Onderdeel14.pin_3, Onderdeel14.pin_5, Onderdeel15.pin_3, Onderdeel15.pin_5, J5.pin2, R16.Pin_0
  3.3V-P3: Onderdeel10.pin_4, Onderdeel10.pin_6, R10.Pin_0, J4.pin5
  SEGA-P3: Onderdeel11.pin_2, J4.pin6
  N9: Onderdeel11.pin_4, Onderdeel11.pin_6, R10.Pin_1, R11.Pin_0
  SEGF-P3: Onderdeel12.pin_2, J4.pin7
  N10: Onderdeel12.pin_4, Onderdeel12.pin_6, R11.Pin_1, R12.Pin_0
  SEGC-P3: Onderdeel13.pin_2, J4.pin4
  N11: Onderdeel13.pin_4, Onderdeel13.pin_6, R12.Pin_1, R13.Pin_0
  SEGE-P3: Onderdeel14.pin_2, J4.pin2
  N12: Onderdeel14.pin_4, Onderdeel14.pin_6, R13.Pin_1, R14.Pin_0
  SEGG-P3: Onderdeel15.pin_2, J4.pin3
  N13: Onderdeel15.pin_4, Onderdeel15.pin_6, R14.Pin_1, R15.Pin_1
  GND-P3: J5.pin1, R15.Pin_0, R16.Pin_1

custom parts:
  LED Tactile Button 12mm: A LED tactile switch
