# Fritzing sketch panel4 (saved by Fritzing 0.9.5d)
circuit board: 9.73986cm x 4cm
breadboards: 1

parts:
  Onderdeel1 = LED Tactile Button 12mm [part_number=BOB-10467]
  Onderdeel2 = LED Tactile Button 12mm [part_number=BOB-10467]
  Onderdeel3 = LED Tactile Button 12mm [part_number=BOB-10467]
  Onderdeel4 = LED Tactile Button 12mm [part_number=BOB-10467]
  Onderdeel5 = LED Tactile Button 12mm [part_number=BOB-10467]
  Onderdeel6 = LED Tactile Button 12mm [part_number=BOB-10467]
  Onderdeel7 = LED Tactile Button 12mm [part_number=BOB-10467]
  Onderdeel8 = LED Tactile Button 12mm [part_number=BOB-10467]
  Onderdeel9 = LED Tactile Button 12mm [part_number=BOB-10467]
  J1 = female pin header, 8 pins [form="♀ (female)"]
  R1 = Resistor [tolerance=±5% resistance=220 package=THT]
  R2 = Resistor [tolerance=±5% resistance=220 package=THT]
  R3 = Resistor [tolerance=±5% resistance=220 package=THT]
  R4 = Resistor [tolerance=±5% resistance=220 package=THT]
  R5 = Resistor [tolerance=±5% resistance=220 package=THT]
  R6 = Resistor [tolerance=±5% resistance=220 package=THT]
  R7 = Resistor [tolerance=±5% resistance=220 package=THT]
  R8 = Resistor [tolerance=±5% resistance=220 package=THT]
  R9 = Resistor [tolerance=±5% resistance=220 package=THT]
  J2 = female pin header, 2 pins [form="♀ (female)"]

nets:
  N1: Onderdeel1.pin_1, Onderdeel2.pin_1, Onderdeel3.pin_1, Onderdeel4.pin_1, Onderdeel5.pin_1, J1.pin8
  N2: Onderdeel1.pin_2, J1.pin3
  N3: Onderdeel1.pin_3, Onderdeel2.pin_3, Onderdeel2.pin_5, Onderdeel3.pin_3, Onderdeel3.pin_5, Onderdeel4.pin_3, Onderdeel4.pin_5, Onderdeel5.pin_3, Onderdeel5.pin_5, Onderdeel6.pin_5, Onderdeel7.pin_3, Onderdeel7.pin_5, Onderdeel8.pin_3, Onderdeel8.pin_5, Onderdeel9.pin_3, Onderdeel9.pin_5, J2.pin2
  N4: Onderdeel1.pin_4, R8.Pin_1, R9.Pin_1
  N5: Onderdeel2.pin_2, Onderdeel6.pin_2, J1.pin2
  N6: Onderdeel2.pin_4, Onderdeel2.pin_6, R7.Pin_1, R8.Pin_0
  N7: Onderdeel3.pin_2, Onderdeel7.pin_2, J1.pin4
  N8: Onderdeel3.pin_4, Onderdeel3.pin_6, R6.Pin_1, R7.Pin_0
  N9: Onderdeel4.pin_2, Onderdeel8.pin_2, J1.pin7
  N10: Onderdeel4.pin_4, Onderdeel4.pin_6, R5.Pin_1, R6.Pin_0
  N11: Onderdeel5.pin_2, Onderdeel9.pin_2, J1.pin6
  N12: Onderdeel5.pin_4, Onderdeel5.pin_6, R1.Pin_0, R5.Pin_0
  N13: Onderdeel6.pin_1, Onderdeel7.pin_1, Onderdeel8.pin_1, Onderdeel9.pin_1, J1.pin1
  N14: Onderdeel6.pin_4, Onderdeel6.pin_6, J1.pin5, R4.Pin_1
  N15: Onderdeel7.pin_4, Onderdeel7.pin_6, R2.Pin_1, R4.Pin_0
  N16: Onderdeel8.pin_4, Onderdeel8.pin_6, R2.Pin_0, R3.Pin_1
  N17: Onderdeel9.pin_4, Onderdeel9.pin_6, R1.Pin_1, R3.Pin_0
  N18: R9.Pin_0, J2.pin1

custom parts:
  LED Tactile Button 12mm: A LED tactile switch
