# Fritzing sketch panel6 (saved by Fritzing 0.9.5d)
circuit board: 6.1cm x 10cm
breadboards: 1

parts:
  Onderdeel2 = LED Tactile Button 12mm [part_number=BOB-10467]
  Onderdeel3 = LED Tactile Button 12mm [part_number=BOB-10467]
  Onderdeel5 = LED Tactile Button 12mm [part_number=BOB-10467]
  Onderdeel6 = LED Tactile Button 12mm [part_number=BOB-10467]
  Onderdeel7 = LED Tactile Button 12mm [part_number=BOB-10467]
  Onderdeel8 = LED Tactile Button 12mm [part_number=BOB-10467]
  Onderdeel9 = LED Tactile Button 12mm [part_number=BOB-10467]
  Onderdeel10 = LED Tactile Button 12mm [part_number=BOB-10467]
  Onderdeel11 = LED Tactile Button 12mm [part_number=BOB-10467]
  R1 = Resistor [tolerance=±5% resistance=220 package=THT]
  R2 = Resistor [tolerance=±5% resistance=220 package=THT]
  R3 = Resistor [tolerance=±5% resistance=220 package=THT]
  to_Panel_#1 = female pin header, 8 pins [form="♀ (female)"]
  R4 = Resistor [tolerance=±5% resistance=220 package=THT]
  R5 = Resistor [tolerance=±5% resistance=220 package=THT]
  R6 = Resistor [tolerance=±5% resistance=220 package=THT]
  R7 = Resistor [tolerance=±5% resistance=220 package=THT]
  R8 = Resistor [tolerance=±5% resistance=220 package=THT]
  to_Teensy = female pin header, 2 pins [form="♀ (female)"]
  R9 = Resistor [tolerance=±5% resistance=220 package=THT]
  R10 = Resistor [tolerance=±5% resistance=1M package=THT]

nets:
  DIG7: Onderdeel2.pin_1, Onderdeel6.pin_1, Onderdeel8.pin_1, Onderdeel10.pin_1, to_Panel_#1.pin8
  SEGE: Onderdeel2.pin_2, Onderdeel3.pin_2, to_Panel_#1.pin2
  Btn-P6: Onderdeel2.pin_3, Onderdeel2.pin_5, Onderdeel3.pin_3, Onderdeel5.pin_3, Onderdeel5.pin_5, Onderdeel6.pin_3, Onderdeel6.pin_5, Onderdeel7.pin_3, Onderdeel7.pin_5, Onderdeel8.pin_3, Onderdeel8.pin_5, Onderdeel9.pin_3, Onderdeel9.pin_5, Onderdeel10.pin_3, Onderdeel10.pin_5, Onderdeel11.pin_3, Onderdeel11.pin_5, to_Teensy.pin2, R10.Pin_1
  3.3V: Onderdeel2.pin_4, Onderdeel2.pin_6, to_Panel_#1.pin5, R8.Pin_0
  DIG5: Onderdeel3.pin_1, Onderdeel5.pin_1, Onderdeel7.pin_1, Onderdeel9.pin_1, Onderdeel11.pin_1, to_Panel_#1.pin1
  N1: Onderdeel3.pin_4, Onderdeel3.pin_6, R1.Pin_0, R9.Pin_0
  SEGC: Onderdeel5.pin_2, Onderdeel6.pin_2, to_Panel_#1.pin4
  N2: Onderdeel5.pin_4, Onderdeel5.pin_6, R2.Pin_1, R3.Pin_0
  N3: Onderdeel6.pin_4, Onderdeel6.pin_6, R6.Pin_0, R7.Pin_1
  SEGG: Onderdeel7.pin_2, Onderdeel8.pin_2, to_Panel_#1.pin3
  N4: Onderdeel7.pin_4, Onderdeel7.pin_6, R1.Pin_1, R2.Pin_0
  N5: Onderdeel8.pin_4, Onderdeel8.pin_6, R7.Pin_0, R8.Pin_1
  SEGA: Onderdeel9.pin_2, Onderdeel10.pin_2, to_Panel_#1.pin6
  N6: Onderdeel9.pin_4, Onderdeel9.pin_6, R3.Pin_1, R4.Pin_0
  N7: Onderdeel10.pin_4, Onderdeel10.pin_6, R5.Pin_1, R6.Pin_1
  SEGF: Onderdeel11.pin_2, to_Panel_#1.pin7
  N8: Onderdeel11.pin_4, Onderdeel11.pin_6, R4.Pin_1, R5.Pin_0
  GND: to_Teensy.pin1, R9.Pin_1, R10.Pin_0

custom parts:
  LED Tactile Button 12mm: A LED tactile switch
