# Fritzing sketch teensy-oled (saved by Fritzing 0.9.5d)
breadboards: 1

parts:
  OLED1 = OLED 128x64 I2C Monochrome Display
  Teensy1 = Teensy 4.0
  R1 = Resistor [tolerance=±5% resistance=10k package=THT]
  R2 = Resistor [tolerance=±5% resistance=10k package=THT]

nets:
  GND: OLED1.GND, Teensy1.pin_1, Teensy1.pin_32
  3.3V: OLED1.VDD, Teensy1.pin_31, R1.Pin_1, R2.Pin_1
  SCL: OLED1.SCK, Teensy1.pin_26, R1.Pin_0
  SDA: OLED1.SDA, Teensy1.pin_25, R2.Pin_0

custom parts:
  Teensy 4.0: The Teensy is a complete USB-based microcontoller development system, in a very small footprint, capable of implementing many types of projects. All programming is done via the USB port. No special programmer is needed, only a standard micro-USB cable and a PC or Macintosh with a USB port.
