# Fritzing sketch panel2-5 (saved by Fritzing 0.9.5d)
circuit board: 11.5826cm x 8.25529cm
breadboards: 1

parts:
  Onderdeel1 = LED Tactile Button 12mm [part_number=BOB-10467]
  Onderdeel2 = LED Tactile Button 12mm [part_number=BOB-10467]
  Onderdeel3 = LED Tactile Button 12mm [part_number=BOB-10467]
  Onderdeel4 = LED Tactile Button 12mm [part_number=BOB-10467]
  Onderdeel5 = LED Tactile Button 12mm [part_number=BOB-10467]
  Onderdeel6 = LED Tactile Button 12mm [part_number=BOB-10467]
  J1 = female pin header, 8 pins [form="♀ (female)"]
  R1 = Resistor [tolerance=±5% resistance=220 package=THT]
  R2 = Resistor [tolerance=±5% resistance=220 package=THT]
  R3 = Resistor [tolerance=±5% resistance=220 package=THT]
  R4 = Resistor [tolerance=±5% resistance=220 package=THT]
  R5 = Resistor [tolerance=±5% resistance=220 package=THT]
  J2 = female pin header, 2 pins [form="♀ (female)"]
  R6 = Resistor [tolerance=±5% resistance=220 package=THT]
  R7 = Resistor [tolerance=±5% resistance=100k package=THT]
  Onderdeel7 = LED Tactile Button 12mm [part_number=BOB-10467]
  Onderdeel8 = LED Tactile Button 12mm [part_number=BOB-10467]
  Onderdeel9 = LED Tactile Button 12mm [part_number=BOB-10467]
  Onderdeel10 = LED Tactile Button 12mm [part_number=BOB-10467]
  Onderdeel11 = LED Tactile Button 12mm [part_number=BOB-10467]
  R8 = Resistor [tolerance=±5% resistance=220 package=THT]
  R9 = Resistor [tolerance=±5% resistance=220 package=THT]
  R10 = Resistor [tolerance=±5% resistance=220 package=THT]
  R11 = Resistor [tolerance=±5% resistance=220 package=THT]
  J5 = female pin header, 2 pins [form="♀ (female)"]
  R12 = Resistor [tolerance=±5% resistance=220 package=THT]
  R13 = Resistor [tolerance=±5% resistance=100k package=THT]
  J6 = female pin header, 8 pins [form="♀ (female)"]
  J7 = female pin header, 15 pins [form="♀ (female)"]  # not connected
  J8 = female pin header, 15 pins [form="♀ (female)"]  # not connected
  J9 = female pin header, 17 pins [form="♀ (female)"]  # not connected
  J10 = female pin header, 17 pins [form="♀ (female)"]  # not connected
  J3 = female pin header, 32 pins [form="♀ (female)"]  # not connected
  J4 = female pin header, 45 pins [form="♀ (female)"]  # not connected
  R14 = TRIMPOT [package=3362u-2]
  R15 = TRIMPOT [package=3362u-2]

nets:
  DIG4: Onderdeel1.pin_1, Onderdeel2.pin_1, Onderdeel3.pin_1, Onderdeel4.pin_1, Onderdeel5.pin_1, Onderdeel6.pin_1, R14.CW
  SEGC: Onderdeel1.pin_2, J1.pin4
  3.3V: Onderdeel1.pin_3, Onderdeel1.pin_5, J1.pin5, R4.Pin_1
  Btn-P5: Onderdeel1.pin_4, Onderdeel1.pin_6, Onderdeel2.pin_4, Onderdeel2.pin_6, Onderdeel3.pin_4, Onderdeel3.pin_6, Onderdeel4.pin_5, Onderdeel5.pin_3, Onderdeel5.pin_5, Onderdeel6.pin_3, Onderdeel6.pin_5, J2.pin1, R7.Pin_0
  SEGG: Onderdeel2.pin_2, J1.pin3
  N1: Onderdeel2.pin_3, Onderdeel2.pin_5, R3.Pin_1, R4.Pin_0
  SEGB: Onderdeel3.pin_2, J1.pin8
  N2: Onderdeel3.pin_3, Onderdeel3.pin_5, R3.Pin_0, R6.Pin_0
  SEGE: Onderdeel4.pin_2, J1.pin2
  N3: Onderdeel4.pin_4, Onderdeel4.pin_6, R1.Pin_0, R2.Pin_1
  SEGF: Onderdeel5.pin_2, J1.pin7
  N4: Onderdeel5.pin_4, Onderdeel5.pin_6, R2.Pin_0, R6.Pin_1
  SEGA: Onderdeel6.pin_2, J1.pin6
  N5: Onderdeel6.pin_4, Onderdeel6.pin_6, R1.Pin_1, R5.Pin_1
  N6: J1.pin1, R14.WIPER
  GND: R5.Pin_0, J2.pin2, R7.Pin_1
  DIG1: Onderdeel7.pin_1, Onderdeel8.pin_1, Onderdeel9.pin_1, Onderdeel10.pin_1, Onderdeel11.pin_1, R15.WIPER
  SEGA-P2: Onderdeel7.pin_2, J6.pin6
  Btn-P2: Onderdeel7.pin_3, Onderdeel7.pin_5, Onderdeel8.pin_3, Onderdeel8.pin_5, Onderdeel9.pin_3, Onderdeel9.pin_5, Onderdeel10.pin_3, Onderdeel10.pin_5, Onderdeel11.pin_3, Onderdeel11.pin_5, J5.pin1, R13.Pin_1
  N7: Onderdeel7.pin_4, Onderdeel7.pin_6, R8.Pin_0, R9.Pin_1
  SEGB-P2: Onderdeel8.pin_2, J6.pin8
  3.3V-P2: Onderdeel8.pin_4, Onderdeel8.pin_6, R8.Pin_1, J6.pin5
  SEGF-P2: Onderdeel9.pin_2, J6.pin7
  N8: Onderdeel9.pin_4, Onderdeel9.pin_6, R9.Pin_0, R10.Pin_1
  SEGG-P2: Onderdeel10.pin_2, J6.pin3
  N9: Onderdeel10.pin_4, Onderdeel10.pin_6, R10.Pin_0, R11.Pin_1
  SEGE-P2: Onderdeel11.pin_2, J6.pin2
  N10: Onderdeel11.pin_4, Onderdeel11.pin_6, R11.Pin_0, R12.Pin_0
  GND-P2: J5.pin2, R12.Pin_1, R13.Pin_0
  N11: J6.pin1, R15.CW
  SEGC-P2: J6.pin4

custom parts:
  LED Tactile Button 12mm: A LED tactile switch
