# Fritzing sketch panel5 (saved by Fritzing 0.9.5d)
circuit board: 5.95838cm x 6.0191cm
breadboards: 1

parts:
  Onderdeel1 = LED Tactile Button 12mm [part_number=BOB-10467]
  Onderdeel2 = LED Tactile Button 12mm [part_number=BOB-10467]
  Onderdeel3 = LED Tactile Button 12mm [part_number=BOB-10467]
  Onderdeel4 = LED Tactile Button 12mm [part_number=BOB-10467]
  Onderdeel5 = LED Tactile Button 12mm [part_number=BOB-10467]
  Onderdeel6 = LED Tactile Button 12mm [part_number=BOB-10467]
  J1 = female pin header, 8 pins [form="♀ (female)"]
  R1 = Resistor [tolerance=±5% resistance=220 package=THT]
  R2 = Resistor [tolerance=±5% resistance=220 package=THT]
  R3 = Resistor [tolerance=±5% resistance=220 package=THT]
  R4 = Resistor [tolerance=±5% resistance=220 package=THT]
  R5 = Resistor [tolerance=±5% resistance=220 package=THT]
  J2 = female pin header, 2 pins [form="♀ (female)"]
  R6 = Resistor [tolerance=±5% resistance=220 package=THT]
  R7 = Resistor [tolerance=±5% resistance=100k package=THT]
  J3 = female pin header, 23 pins [form="♀ (female)"]  # not connected
  J4 = female pin header, 23 pins [form="♀ (female)"]  # not connected

nets:
  DIG4: Onderdeel1.pin_1, Onderdeel2.pin_1, Onderdeel3.pin_1, Onderdeel4.pin_1, Onderdeel5.pin_1, Onderdeel6.pin_1, J1.pin1
  SEGC: Onderdeel1.pin_2, J1.pin4
  3.3V: Onderdeel1.pin_3, Onderdeel1.pin_5, J1.pin5, R4.Pin_1
  Btn-P5: Onderdeel1.pin_4, Onderdeel1.pin_6, Onderdeel2.pin_4, Onderdeel2.pin_6, Onderdeel3.pin_4, Onderdeel3.pin_6, Onderdeel4.pin_5, Onderdeel5.pin_3, Onderdeel5.pin_5, Onderdeel6.pin_3, Onderdeel6.pin_5, J2.pin1, R7.Pin_0
  SEGG: Onderdeel2.pin_2, J1.pin3
  N1: Onderdeel2.pin_3, Onderdeel2.pin_5, R3.Pin_1, R4.Pin_0
  SEGB: Onderdeel3.pin_2, J1.pin8
  N2: Onderdeel3.pin_3, Onderdeel3.pin_5, R3.Pin_0, R6.Pin_0
  SEGE: Onderdeel4.pin_2, J1.pin2
  N3: Onderdeel4.pin_4, Onderdeel4.pin_6, R1.Pin_0, R2.Pin_1
  SEGF: Onderdeel5.pin_2, J1.pin7
  N4: Onderdeel5.pin_4, Onderdeel5.pin_6, R2.Pin_0, R6.Pin_1
  SEGA: Onderdeel6.pin_2, J1.pin6
  N5: Onderdeel6.pin_4, Onderdeel6.pin_6, R1.Pin_1, R5.Pin_1
  GND: R5.Pin_0, J2.pin2, R7.Pin_1

custom parts:
  LED Tactile Button 12mm: A LED tactile switch
